// Logisim project CPU.circ as structural Verilog
module main (
);

  wire and_1_out, BUSREQ, BUSWRITE, clk, comparator_2_eq, comparator_3_eq, controlled_buffer_2_out,
       cpu_1_ramoe, cpu_1_ramwe, HLT, IOSEL, nor_1_out, not_1_out, RESET, rgb_video_1_p2, rgb_video_1_p5,
       rgb_video_2_p1, rgb_video_2_p2, RW, t_ff_1_qn;
  wire [3:0] a, b, c, d, e, f, rgb_video_2_p5, SP;
  wire [4:0] rgb_video_1_p6, rgb_video_1_p7;
  wire [6:0] ASCII;
  wire [7:0] INSTOP, INSTRUCTION, rgb_video_2_p3, rgb_video_2_p4;
  wire [15:0] ADDR, bank_1_out_3, controlled_buffer_1_out, cpu_1_ramaddr, cpu_1_ramin, DATA, IO,
       multiplexer_1_out, PC, ram_1_dout, undriven;
  wire [23:0] rgb_video_1_p8;

  LED led_1 (.in(HLT));
  Clock clock_1 (.out(clk));
  Keyboard keyboard_1 (.clk(clk), .re(BUSREQ), .data(ASCII));  // open: clr, avail
  LED led_2 (.in(BUSWRITE));
  Button button_1 (.out(RESET));
  BANK bank_1 (.PC(PC), .ADDR(ADDR), .out_3({INSTRUCTION, INSTOP, bank_1_out_3}));
  Hex_Digit_Display hex_digit_display_1 (.value({1'b0, ASCII[6:4]}));  // open: dp
  Hex_Digit_Display hex_digit_display_2 (.value(ASCII[3:0]));  // open: dp
  Hex_Digit_Display hex_digit_display_3 (.value(PC[15:12]));  // open: dp
  LED led_3 (.in(BUSREQ));
  Comparator #(.width(16)) comparator_1 (.a(undriven), .b(16'h4), .eq(IOSEL));  // open: gt, lt
  Hex_Digit_Display hex_digit_display_4 (.value(PC[11:8]));  // open: dp
  Hex_Digit_Display hex_digit_display_5 (.value(PC[7:4]));  // open: dp
  LED led_4 (.in(RW));
  Multiplexer #(.width(16)) multiplexer_1 (.in0({16{1'b0}}), .in1(undriven), .out(multiplexer_1_out), .sel(IOSEL));
  // LedBar #(.inputtype("row"), .matrixcols(16)) ledbar_1: pin names not known; wires that end beside it: multiplexer_1_out
  DipSwitch #(.number(16)) dipswitch_1 (
    .sw1(IO[15]), .sw2(IO[14]), .sw3(IO[13]), .sw4(IO[12]), .sw5(IO[11]), .sw6(IO[10]), .sw7(IO[9]),
    .sw8(IO[8]), .sw9(IO[7]), .sw10(IO[6]), .sw11(IO[5]), .sw12(IO[4]), .sw13(IO[3]), .sw14(IO[2]),
    .sw15(IO[1]), .sw16(IO[0]));
  assign controlled_buffer_1_out = comparator_2_eq ? {{9{1'b0}}, ASCII} : 16'bz;  // Controlled_Buffer controlled_buffer_1
  Comparator #(.mode("unsigned"), .width(16)) comparator_2 (
    .a(ADDR), .b(16'hfffe), .eq(comparator_2_eq));  // open: gt, lt
  Hex_Digit_Display hex_digit_display_6 (.value(PC[3:0]));  // open: dp
  Hex_Digit_Display hex_digit_display_7 (.value(INSTRUCTION[7:4]));  // open: dp
  Hex_Digit_Display hex_digit_display_8 (.value(DATA[15:12]));  // open: dp
  Hex_Digit_Display hex_digit_display_9 (.value(DATA[11:8]));  // open: dp
  // _7_Segment_Display 7_segment_display_1: pin names not known; wires that end beside it: d, e
  // BCD_to_7_Segment_decoder bcd_to_7_segment_decoder_1: pin names not known
  Hex_Digit_Display hex_digit_display_10 (.value(INSTRUCTION[3:0]));  // open: dp
  Hex_Digit_Display hex_digit_display_11 (.value(INSTOP[7:4]));  // open: dp
  Hex_Digit_Display hex_digit_display_12 (.value(DATA[7:4]));  // open: dp
  Hex_Digit_Display hex_digit_display_13 (.value(DATA[3:0]));  // open: dp
  // _7_Segment_Display 7_segment_display_2: pin names not known; wires that end beside it: e, f
  // _7_Segment_Display 7_segment_display_3: pin names not known; wires that end beside it: f, a
  // BCD_to_7_Segment_decoder bcd_to_7_segment_decoder_2: pin names not known
  // BCD_to_7_Segment_decoder bcd_to_7_segment_decoder_3: pin names not known
  CPU cpu_1 (
    .DATAIN(controlled_buffer_1_out), .clk(clk), .ROMIN({INSTRUCTION, INSTOP, bank_1_out_3}),
    .RAMOUT(ram_1_dout), .Reset(RESET), .RW(RW), .ROMADDR(PC), .RAMIN(cpu_1_ramin), .RAMADDR(cpu_1_ramaddr),
    .RAMWE(cpu_1_ramwe), .RAMOE(cpu_1_ramoe), .Dataout(DATA), .ADDR(ADDR), .BUSREQ(BUSREQ),
    .BUSWRITE(BUSWRITE), .HLT(HLT), .POINTER(SP));
  Hex_Digit_Display hex_digit_display_14 (.value(INSTOP[3:0]));  // open: dp
  Hex_Digit_Display hex_digit_display_15 (.value(ADDR[15:12]));  // open: dp
  Hex_Digit_Display hex_digit_display_16 (.value(ADDR[11:8]));  // open: dp
  // _7_Segment_Display 7_segment_display_4: pin names not known; wires that end beside it: a, b
  // BCD_to_7_Segment_decoder bcd_to_7_segment_decoder_4: pin names not known
  Hex_Digit_Display hex_digit_display_17 (.value(SP));  // open: dp
  Hex_Digit_Display hex_digit_display_18 (.value(ADDR[7:4]));  // open: dp
  Hex_Digit_Display hex_digit_display_19 (.value(ADDR[3:0]));  // open: dp
  // _7_Segment_Display 7_segment_display_5: pin names not known; wires that end beside it: b, c
  _7_Segment_Display u_7_segment_display_6 ();  // open: g, f, a, b, e, d, c, dp
  // BCD_to_7_Segment_decoder bcd_to_7_segment_decoder_5: pin names not known
  // BCD_to_7_Segment_decoder bcd_to_7_segment_decoder_6: pin names not known
  RAM #(.addrWidth(16), .clearpin("true"), .dataWidth(16)) ram_1 (
    .addr(cpu_1_ramaddr), .we(cpu_1_ramwe), .oe(cpu_1_ramoe), .clk(clk), .din(cpu_1_ramin),
    .dout(ram_1_dout), .clr(t_ff_1_qn));
  and and_1 (and_1_out, controlled_buffer_2_out, comparator_3_eq);
  T_Flip_Flop t_ff_1 (.T(t_ff_1_qn), .clk(clk), .Qn(t_ff_1_qn));  // open: Q, reset, preset
  assign controlled_buffer_2_out = nor_1_out ? BUSWRITE : 1'bz;  // Controlled_Buffer controlled_buffer_2
  Comparator #(.mode("unsigned"), .width(7)) comparator_3 (
    .a(DATA[6:0]), .b(7'b0000111), .eq(comparator_3_eq));  // open: gt, lt
  nor nor_1 (nor_1_out, ADDR[1], ADDR[2], ADDR[3], ADDR[4], ADDR[5], ADDR[6], ADDR[7], ADDR[8], ADDR[9], ADDR[10], ADDR[11], ADDR[12], ADDR[13], ADDR[14], ADDR[0]);
  // RGB_Video #(.height(32), .scale(7), .width(32)) rgb_video_1: pin names not known; wires that end beside it: RESET, rgb_video_1_p2, RESET, clk, rgb_video_1_p5, rgb_video_1_p6, rgb_video_1_p7, rgb_video_1_p8
  TTY tty_1 (.data(DATA[6:0]), .clk(clk), .we(controlled_buffer_2_out), .clr(rgb_video_1_p2));
  Multiplexer multiplexer_2 (.in0(RESET), .in1(and_1_out), .out(rgb_video_1_p2), .sel(and_1_out));
  assign controlled_buffer_2_out = not_1_out ? 1'b0 : 1'bz;  // Controlled_Buffer controlled_buffer_3
  not not_1 (not_1_out, nor_1_out);
  GPU gpu_1 (
    .S({16{1'b0}}), .W(BUSWRITE), .ADDR(ADDR), .DATA(DATA), .R(RESET), .clk(clk), .X(rgb_video_1_p6),
    .Y(rgb_video_1_p7), .RGBOUT(rgb_video_1_p8), .WRITE(rgb_video_1_p5));  // open: PROGRAM
  // RGB_Video #(.cursor("No Cursor"), .height(256), .width(256)) rgb_video_2: pin names not known; wires that end beside it: rgb_video_2_p1, rgb_video_2_p2, rgb_video_2_p3, rgb_video_2_p4, rgb_video_2_p5
  BCDTO7SEG bcdto7seg_1 (
    .DATAIN(DATA), .ENA(BUSWRITE), .CLK(clk), .in_4(ADDR), .out_5(a), .out_6(b), .out_7(c), .out_8(d),
    .out_9(e), .out_10(f));
  GPUmkII gpumkii_1 (
    .DATA(DATA), .clk(clk), .WE(rgb_video_2_p2), .CLR(rgb_video_2_p5), .x(rgb_video_2_p3),
    .y(rgb_video_2_p4), .OUTCLK(rgb_video_2_p1));  // open: RD, WR
endmodule

module ALU (
  input  [2:0] MUX,
  input  [7:0] CPUBUS,
  input  [7:0] ACC,
  output [7:0] ALUOUT
);

  wire [7:0] adder_1_out, and_1_out, multiplier_1_out, negator_1_out, not_1_out, or_1_out, subtractor_1_out,
       undriven;

  Adder adder_1 (.a(ACC), .b(CPUBUS), .out(adder_1_out));  // open: cin, cout
  Subtractor subtractor_1 (.a(ACC), .b(CPUBUS), .out(subtractor_1_out));  // open: bin, bout
  Multiplier multiplier_1 (.a(ACC), .b(CPUBUS), .out(multiplier_1_out));  // open: cin, cout
  Negator negator_1 (.in(ACC), .out(negator_1_out));
  assign and_1_out = ACC & CPUBUS;  // AND_Gate and_1, 8 bits wide
  assign or_1_out = ACC | CPUBUS;  // OR_Gate or_1, 8 bits wide
  assign not_1_out = ~ACC;  // NOT_Gate not_1, 8 bits wide
  Multiplexer #(.select(3), .width(8)) multiplexer_1 (
    .in0(adder_1_out), .in1(subtractor_1_out), .in2(multiplier_1_out), .in3(undriven), .in4(negator_1_out),
    .in5(and_1_out), .in6(or_1_out), .in7(not_1_out), .out(ALUOUT), .sel(MUX));
endmodule

module COMPARE (
  input  [7:0] ACC,
  input  [1:0] INST,
  input  OE,
  output Output_1
);

  wire comparator_1_eq, comparator_1_gt, not_1_out;

  Comparator comparator_1 (.a(ACC), .b({8{1'b0}}), .gt(comparator_1_gt), .eq(comparator_1_eq));  // open: lt
  not not_1 (not_1_out, comparator_1_eq);
  Multiplexer #(.enable("true"), .select(2)) multiplexer_1 (
    .in0(1'b1), .in1(comparator_1_gt), .in2(not_1_out), .in3(comparator_1_eq), .out(Output_1), .sel(INST),
    .en(OE));
endmodule

module CONTROL (
  input  RESET,
  input  [31:0] INSTRUCTION,
  input  clk,
  output [3:0] REGOUTSEL,
  output [3:0] REGINSEL,
  output CPUSEL,
  output [15:0] CPU8,
  output [1:0] COMPARE,
  output NOP,
  output CONTROLOE,
  output REGCONTROL,
  output [2:0] ALU,
  output ALUOE,
  output Stack,
  output HLT
);

  wire and_1_out, decoder_1_out3;
  wire [15:0] demultiplexer_1_out1;
  wire [31:0] demultiplexer_1_out0;

  J_K_Flip_Flop j_k_ff_1 (.J(decoder_1_out3), .K(RESET), .clk(clk), .Qn(HLT));  // open: Q, preset, reset
  Demultiplexer #(.width(32)) demultiplexer_1 (
    .out0({demultiplexer_1_out0[31:27], ALU, REGINSEL, REGOUTSEL, demultiplexer_1_out0[15:0]}),
    .out1({CPU8, demultiplexer_1_out1}), .in(INSTRUCTION), .sel(CPUSEL));
  and and_1 (and_1_out, ALU[0], ALU[1], ALU[2], demultiplexer_1_out0[27], demultiplexer_1_out0[29], demultiplexer_1_out0[30], demultiplexer_1_out0[31], demultiplexer_1_out0[28]);
  Decoder #(.select(3)) decoder_1 (
    .out0(NOP), .out1(Stack), .out2(CONTROLOE), .out3(decoder_1_out3), .out4(REGCONTROL), .out6(ALUOE),
    .sel(demultiplexer_1_out0[31:29]));  // open: out5, out7, en
  J_K_Flip_Flop j_k_ff_2 (.J(and_1_out), .K(RESET), .clk(clk), .Q(CPUSEL));  // open: Qn, preset, reset
  Hex_Digit_Display Hex_Digit_Display_1 (.value(REGINSEL));  // open: dp
  Hex_Digit_Display Hex_Digit_Display_2 (.value(REGOUTSEL));  // open: dp

  assign COMPARE = ALU[1:0];
endmodule

module CPU (
  input  [15:0] DATAIN,
  input  clk,
  input  [31:0] ROMIN,
  input  [15:0] RAMOUT,
  input  Reset,
  output RW,
  output [15:0] ROMADDR,
  output [15:0] RAMIN,
  output [15:0] RAMADDR,
  output RAMWE,
  output RAMOE,
  output [15:0] Dataout,
  output [15:0] ADDR,
  output BUSREQ,
  output BUSWRITE,
  output HLT,
  output [3:0] POINTER
);

  wire ALU16_1_output_1, and_1_out, comparator_1_eq, CONTROL_1_aluoe, CONTROL_1_controloe, CONTROL_1_cpusel,
       CONTROL_1_hlt, CONTROL_1_nop, CONTROL_1_regcontrol, CONTROL_1_stack, CPU8bit_1_ramoe, CPU8bit_1_ramwe,
       multiplexer_4_out, not_2_out, or_1_out, POP, REGCONTROLLER_1_imm, REGCONTROLLER_1_ramoe,
       REGCONTROLLER_1_ramwe, REGCONTROLLER_1_regout, t_ff_1_q, t_ff_1_qn, undriven_2;
  wire [1:0] CONTROL_1_compare, REGCONTROLLER_1_busreq;
  wire [2:0] CONTROL_1_alu;
  wire [3:0] CONTROL_1_reginsel, CONTROL_1_regoutsel;
  wire [7:0] CPU8bit_1_ramdata, CPU8bit_1_romaddr, demultiplexer_1_out1, demultiplexer_1_out1_2;
  wire [15:0] ACC, ALU16_1_aluout, CONTROL_1_cpu8, counter_1_q, demultiplexer_1_out0, MMU_1_memaddr,
       multiplexer_2_out, multiplexer_7_out, multiplexer_9_out, REGCONTROLLER_1_output_bus_1,
       REGCONTROLLER_1_ramaddrout, REGCONTROLLER_1_reg0, REGCONTROLLER_1_reg1, Stack_1_stackout, undriven;

  or or_1 (or_1_out, t_ff_1_qn, Reset);
  nor nor_1 (RW, RAMOE, REGCONTROLLER_1_ramoe, 1'b0, REGCONTROLLER_1_imm, REGCONTROLLER_1_regout, REGCONTROLLER_1_imm, RAMWE);
  T_Flip_Flop t_ff_1 (.T(or_1_out), .clk(clk), .Q(t_ff_1_q), .Qn(t_ff_1_qn));  // open: reset, preset
  CONTROL CONTROL_1 (
    .RESET(Reset), .INSTRUCTION(ROMIN), .clk(clk), .REGOUTSEL(CONTROL_1_regoutsel),
    .REGINSEL(CONTROL_1_reginsel), .CPUSEL(CONTROL_1_cpusel), .CPU8(CONTROL_1_cpu8),
    .COMPARE(CONTROL_1_compare), .NOP(CONTROL_1_nop), .CONTROLOE(CONTROL_1_controloe),
    .REGCONTROL(CONTROL_1_regcontrol), .ALU(CONTROL_1_alu), .ALUOE(CONTROL_1_aluoe), .Stack(CONTROL_1_stack),
    .HLT(CONTROL_1_hlt));
  assign Dataout = REGCONTROLLER_1_imm ? ROMIN[15:0] : 16'bz;  // Controlled_Buffer controlled_buffer_1
  Multiplexer #(.width(16)) multiplexer_1 (
    .in0(multiplexer_2_out), .in1({CPU8bit_1_ramdata, {8{1'b0}}}), .out(RAMIN), .sel(CONTROL_1_cpusel));
  Multiplexer #(.width(16)) multiplexer_2 (.in0({16{1'b0}}), .in1(Dataout), .out(multiplexer_2_out), .sel(t_ff_1_q));
  not not_1 (HLT, CONTROL_1_hlt);
  assign Dataout = RW ? multiplexer_9_out : 16'bz;  // Controlled_Buffer controlled_buffer_2
  Demultiplexer #(.width(16)) demultiplexer_1 (
    .out0(demultiplexer_1_out0), .out1({demultiplexer_1_out1_2, demultiplexer_1_out1}), .in(RAMOUT),
    .sel(CONTROL_1_cpusel));
  Multiplexer #(.width(16)) multiplexer_3 (
    .in0(REGCONTROLLER_1_ramaddrout), .in1(undriven), .out(RAMADDR), .sel(CONTROL_1_cpusel));
  Multiplexer multiplexer_4 (.in0(CONTROL_1_aluoe), .in1(POP), .out(multiplexer_4_out), .sel(POP));
  CPU8bit CPU8bit_1 (
    .RAMIN(demultiplexer_1_out1_2), .clk(clk), .ROMIN(CONTROL_1_cpu8), .RAMADDR(undriven[15:8]),
    .RAMWE(CPU8bit_1_ramwe), .RAMOE(CPU8bit_1_ramoe), .RAMDATA(CPU8bit_1_ramdata), .ROMADDR(CPU8bit_1_romaddr));  // open: DATAIN, RW, DATAOUT, BUSREQ, ADDR
  Multiplexer multiplexer_5 (.in0(REGCONTROLLER_1_ramoe), .in1(CPU8bit_1_ramoe), .out(RAMOE), .sel(CONTROL_1_cpusel));
  Multiplexer multiplexer_6 (.in0(REGCONTROLLER_1_ramwe), .in1(CPU8bit_1_ramwe), .out(RAMWE), .sel(CONTROL_1_cpusel));
  Stack Stack_1 (
    .StackOE(CONTROL_1_stack), .StackINST(CONTROL_1_compare), .clk(clk), .RESET(t_ff_1_qn), .STACKIN(ACC),
    .POP(POP), .STACKOUT(Stack_1_stackout), .POINTER(POINTER));
  REGCONTROLLER REGCONTROLLER_1 (
    .Datain(Dataout), .ALUOE(multiplexer_4_out), .ALU(multiplexer_7_out), .REGOUTSEL(CONTROL_1_regoutsel),
    .Enable(CONTROL_1_regcontrol), .REGINSEL(CONTROL_1_reginsel), .CLK(clk), .RESET(Reset), .ACCOUT(ACC),
    .REG0(REGCONTROLLER_1_reg0), .REGOUT(REGCONTROLLER_1_regout), .RAMOE(REGCONTROLLER_1_ramoe), .ADDR(ADDR),
    .BUSWRITE(BUSWRITE), .BUSREQ(REGCONTROLLER_1_busreq[0]), .Output_bus_1(REGCONTROLLER_1_output_bus_1),
    .IMM(REGCONTROLLER_1_imm), .RAMWE(REGCONTROLLER_1_ramwe), .REG1(REGCONTROLLER_1_reg1),
    .RAMADDROUT(REGCONTROLLER_1_ramaddrout));
  assign Dataout = REGCONTROLLER_1_regout ? REGCONTROLLER_1_output_bus_1 : 16'bz;  // Controlled_Buffer controlled_buffer_3
  assign Dataout = REGCONTROLLER_1_ramoe ? demultiplexer_1_out0 : 16'bz;  // Controlled_Buffer controlled_buffer_4
  Multiplexer #(.width(16)) multiplexer_7 (
    .in0(ALU16_1_aluout), .in1(Stack_1_stackout), .out(multiplexer_7_out), .sel(POP));
  ALU16 ALU16_1 (
    .MUX(CONTROL_1_alu), .REG3(REGCONTROLLER_1_reg0), .ACC(ACC), .COMPAREINST(CONTROL_1_compare),
    .BRANCHOE(CONTROL_1_controloe), .REG1(REGCONTROLLER_1_reg1), .ALUOUT(ALU16_1_aluout),
    .Output_1(ALU16_1_output_1));
  MMU MMU_1 (.ADDR(ADDR), .DATA(ADDR), .clk(clk), .Reset(undriven_2), .MEMADDR(MMU_1_memaddr));
  Multiplexer multiplexer_8 (.in0(REGCONTROLLER_1_busreq[0]), .in1(1'b0), .out(BUSREQ), .sel(comparator_1_eq));
  Comparator #(.mode("unsigned"), .width(16)) comparator_1 (
    .a(ADDR), .b({16{1'b1}}), .eq(comparator_1_eq));  // open: gt, lt
  Multiplexer #(.select(2), .width(16)) multiplexer_9 (
    .in0({16{1'b0}}), .in1(DATAIN), .in2({16{1'b0}}), .in3(counter_1_q), .out(multiplexer_9_out),
    .sel(REGCONTROLLER_1_busreq));
  Counter #(.max('hffff), .width(16)) counter_1 (
    .load(ALU16_1_output_1), .D(ADDR), .count(CONTROL_1_hlt), .Q(counter_1_q), .clk(clk), .clr(not_2_out));  // open: carry, up
  not not_2 (not_2_out, t_ff_1_q);
  and and_1 (and_1_out, REGCONTROLLER_1_busreq[0], REGCONTROLLER_1_busreq[1]);
  Multiplexer #(.width(16)) multiplexer_10 (
    .in0(counter_1_q), .in1({CPU8bit_1_romaddr, {8{1'b0}}}), .out(ROMADDR), .sel(CONTROL_1_cpusel));
  Comparator #(.mode("unsigned"), .width(16)) comparator_2 (
    .a(ADDR), .b({16{1'b1}}), .eq(REGCONTROLLER_1_busreq[1]));  // open: gt, lt
endmodule

module CPU8bit (
  input  [7:0] DATAIN,
  input  [7:0] RAMIN,
  input  clk,
  input  [15:0] ROMIN,
  output RW,
  output [7:0] RAMADDR,
  output [7:0] DATAOUT,
  output BUSREQ,
  output RAMWE,
  output RAMOE,
  output [7:0] RAMDATA,
  output [7:0] ROMADDR,
  output [7:0] ADDR
);

  wire COMPARE_1_output_1, CONTROL8BIT_1_accoe, CONTROL8BIT_1_accwe, CONTROL8BIT_1_aluoe, CONTROL8BIT_1_boe,
       CONTROL8BIT_1_bwe, CONTROL8BIT_1_controloe, CONTROL8BIT_1_erasea, CONTROL8BIT_1_eraseb,
       CONTROL8BIT_1_ramoe, CONTROL8BIT_1_romwe, multiplexer_2_out, multiplexer_3_out, multiplexer_5_out,
       t_ff_1_qn;
  wire [1:0] CONTROL8BIT_1_compare;
  wire [2:0] CONTROL8BIT_1_alu;
  wire [7:0] ALU_1_aluout, multiplexer_1_out;

  Multiplexer #(.width(8)) multiplexer_1 (.in0({8{1'b0}}), .in1(DATAIN), .out(multiplexer_1_out), .sel(BUSREQ));
  assign DATAOUT = RW ? multiplexer_1_out : 8'bz;  // Controlled_Buffer controlled_buffer_1
  CONTROL8BIT CONTROL8BIT_1 (
    .INSTRUCTION(ROMIN[15:8]), .clk(clk), .ACCWE(CONTROL8BIT_1_accwe), .ROMWE(CONTROL8BIT_1_romwe),
    .ERASEA(CONTROL8BIT_1_erasea), .ACCOE(CONTROL8BIT_1_accoe), .BWE(CONTROL8BIT_1_bwe),
    .BOE(CONTROL8BIT_1_boe), .ERASEB(CONTROL8BIT_1_eraseb), .COMPARE(CONTROL8BIT_1_compare),
    .CONTROLOE(CONTROL8BIT_1_controloe), .ALU(CONTROL8BIT_1_alu), .ALUOE(CONTROL8BIT_1_aluoe),
    .BUSREQ(BUSREQ), .RAMWE(RAMWE), .RAMOE(CONTROL8BIT_1_ramoe));
  COMPARE COMPARE_1 (
    .ACC(RAMDATA), .INST(CONTROL8BIT_1_compare), .OE(CONTROL8BIT_1_controloe), .Output_1(COMPARE_1_output_1));
  nor nor_1 (RW, CONTROL8BIT_1_accoe, CONTROL8BIT_1_boe, CONTROL8BIT_1_aluoe, CONTROL8BIT_1_romwe, CONTROL8BIT_1_ramoe);
  Counter counter_1 (.load(COMPARE_1_output_1), .D(ADDR), .Q(ROMADDR), .clk(clk));  // open: count, carry, up, clr
  assign DATAOUT = CONTROL8BIT_1_boe ? ADDR : 8'bz;  // Controlled_Buffer controlled_buffer_2
  ALU ALU_1 (.MUX(CONTROL8BIT_1_alu), .CPUBUS(ADDR), .ACC(RAMDATA), .ALUOUT(ALU_1_aluout));
  assign DATAOUT = CONTROL8BIT_1_aluoe ? ALU_1_aluout : 8'bz;  // Controlled_Buffer controlled_buffer_3
  assign DATAOUT = CONTROL8BIT_1_romwe ? ROMIN[7:0] : 8'bz;  // Controlled_Buffer controlled_buffer_4
  Register register_1 (.D(DATAOUT), .en(CONTROL8BIT_1_bwe), .clk(clk), .Q(ADDR), .clr(multiplexer_2_out));
  Multiplexer multiplexer_2 (
    .in0(CONTROL8BIT_1_eraseb), .in1(multiplexer_5_out), .out(multiplexer_2_out), .sel(multiplexer_5_out));
  Register register_2 (.D(DATAOUT), .en(CONTROL8BIT_1_accwe), .clk(clk), .Q(RAMDATA), .clr(multiplexer_3_out));
  Multiplexer multiplexer_3 (
    .in0(CONTROL8BIT_1_erasea), .in1(multiplexer_5_out), .out(multiplexer_3_out), .sel(multiplexer_5_out));
  assign DATAOUT = CONTROL8BIT_1_accoe ? RAMDATA : 8'bz;  // Controlled_Buffer controlled_buffer_5
  assign DATAOUT = CONTROL8BIT_1_ramoe ? RAMIN : 8'bz;  // Controlled_Buffer controlled_buffer_6
  Multiplexer multiplexer_4 (.in0(CONTROL8BIT_1_ramoe), .in1(multiplexer_5_out), .out(RAMOE), .sel(multiplexer_5_out));
  Multiplexer multiplexer_5 (.in0(1'b0), .in1(t_ff_1_qn), .out(multiplexer_5_out), .sel(t_ff_1_qn));
  T_Flip_Flop t_ff_1 (.T(t_ff_1_qn), .clk(clk), .Qn(t_ff_1_qn));  // open: Q, reset, preset

  assign RAMADDR = ADDR;

  // Notes on the sheet:
  //   B
  //   ACC
endmodule

module CONTROL8BIT (
  input  [7:0] INSTRUCTION,
  input  clk,
  output ACCWE,
  output ROMWE,
  output ERASEA,
  output ACCOE,
  output BWE,
  output BOE,
  output ERASEB,
  output [1:0] COMPARE,
  output CONTROLOE,
  output [2:0] ALU,
  output ALUOE,
  output BUSREQ,
  output RAMWE,
  output RAMOE
);

  wire and_1_out, and_2_out, and_3_out, and_4_out, and_5_out, and_6_out, decoder_1_out2, decoder_2_out0,
       decoder_2_out1, decoder_2_out2, decoder_3_out0, decoder_3_out1, decoder_3_out2, demultiplexer_2_out0,
       not_1_out, or_2_out, or_5_out;
  wire [1:0] demultiplexer_1_out0, demultiplexer_1_out1, multiplexer_1_out, multiplexer_2_out;
  wire [7:3] register_1_q;

  Register register_1 (.D(INSTRUCTION), .en(1'b1), .clk(clk), .Q({register_1_q, ALU}));  // open: clr
  Decoder #(.select(2)) decoder_1 (
    .out1(CONTROLOE), .out2(decoder_1_out2), .out3(ALUOE), .sel(register_1_q[7:6]));  // open: out0, en
  not not_1 (not_1_out, ALU[2]);
  Demultiplexer #(.width(2)) demultiplexer_1 (
    .out0(demultiplexer_1_out0), .out1(demultiplexer_1_out1), .in(ALU[1:0]), .sel(ALU[2]));
  and and_1 (and_1_out, decoder_1_out2, not_1_out);
  and and_2 (and_2_out, ALU[2], decoder_1_out2);
  Decoder #(.select(2)) decoder_2 (
    .out0(decoder_2_out0), .out1(decoder_2_out1), .out2(decoder_2_out2), .out3(ERASEA),
    .sel(multiplexer_1_out));  // open: en
  Multiplexer #(.width(2)) multiplexer_1 (
    .in0(2'b00), .in1(demultiplexer_1_out0), .out(multiplexer_1_out), .sel(decoder_1_out2));
  Multiplexer #(.width(2)) multiplexer_2 (
    .in0(2'b00), .in1(demultiplexer_1_out1), .out(multiplexer_2_out), .sel(decoder_1_out2));
  and and_3 (and_3_out, and_1_out, decoder_2_out0);
  and and_4 (and_4_out, and_2_out, decoder_3_out0);
  Decoder #(.select(2)) decoder_3 (
    .out0(decoder_3_out0), .out1(decoder_3_out1), .out2(decoder_3_out2), .out3(ERASEB),
    .sel(multiplexer_2_out));  // open: en
  and and_5 (and_5_out, and_1_out, decoder_2_out0);
  or or_1 (ACCOE, decoder_2_out1, decoder_2_out2);
  and and_6 (and_6_out, and_2_out, decoder_3_out0);
  or or_2 (or_2_out, and_3_out, and_4_out);
  or or_3 (BWE, decoder_2_out1, and_6_out);
  or or_4 (BOE, decoder_3_out1, decoder_3_out2);
  or or_5 (or_5_out, ALUOE, decoder_3_out1);
  or or_6 (ACCWE, and_5_out, or_5_out);
  Demultiplexer demultiplexer_2 (.out0(demultiplexer_2_out0), .out1(RAMOE), .in(or_2_out), .sel(register_1_q[3]));
  Demultiplexer demultiplexer_3 (.out0(ROMWE), .out1(BUSREQ), .in(demultiplexer_2_out0), .sel(register_1_q[4]));
  and and_7 (RAMWE, ACCOE, register_1_q[3]);

  assign COMPARE = ALU[1:0];
endmodule

module REGCONTROLLER (
  input  [15:0] Datain,
  input  ALUOE,
  input  [15:0] ALU,
  input  [3:0] REGOUTSEL,
  input  Enable,
  input  [3:0] REGINSEL,
  input  CLK,
  input  RESET,
  output [15:0] ACCOUT,
  output [15:0] REG0,
  output REGOUT,
  output RAMOE,
  output [15:0] ADDR,
  output BUSWRITE,
  output BUSREQ,
  output [15:0] Output_bus_1,
  output IMM,
  output RAMWE,
  output [15:0] REG1,
  output [15:0] RAMADDROUT
);

  wire decoder_1_out0, decoder_1_out1, decoder_1_out2, decoder_1_out3, decoder_1_out4, decoder_1_out5,
       decoder_1_out6, decoder_1_out7, decoder_1_out8, decoder_1_out9, decoder_1_out10, decoder_1_out11,
       decoder_1_out12, decoder_1_out14, decoder_1_out15, decoder_2_out0, decoder_2_out1, decoder_2_out2,
       decoder_2_out3, decoder_2_out4, decoder_2_out5, decoder_2_out6, decoder_2_out7, decoder_2_out8,
       decoder_2_out9, decoder_2_out10, decoder_2_out11, decoder_2_out12, multiplexer_1_out,
       multiplexer_3_out, or_2_out, t_ff_1_qn;
  wire [15:0] multiplexer_2_out, R_2_q, R_3_q, R_4_q, R_5_q, R_6_q, R_7_q, R_8_q, R_9_q;

  Decoder #(.select(4)) decoder_1 (
    .out0(decoder_1_out0), .out1(decoder_1_out1), .out2(decoder_1_out2), .out3(decoder_1_out3),
    .out4(decoder_1_out4), .out5(decoder_1_out5), .out6(decoder_1_out6), .out7(decoder_1_out7),
    .out8(decoder_1_out8), .out9(decoder_1_out9), .out10(decoder_1_out10), .out11(decoder_1_out11),
    .out12(decoder_1_out12), .out13(BUSWRITE), .out14(decoder_1_out14), .out15(decoder_1_out15),
    .sel(REGINSEL), .en(Enable));
  Multiplexer multiplexer_1 (.in0(decoder_1_out2), .in1(ALUOE), .out(multiplexer_1_out), .sel(ALUOE));
  Register #(.width(16)) ACC (.D(Datain), .en(decoder_1_out0), .clk(CLK), .Q(ACCOUT), .clr(multiplexer_3_out));
  Register #(.width(16)) R0 (.D(Datain), .en(decoder_1_out1), .clk(CLK), .Q(REG0), .clr(multiplexer_3_out));
  Register #(.width(16)) R_1 (
    .D(multiplexer_2_out), .en(multiplexer_1_out), .clk(CLK), .Q(REG1), .clr(multiplexer_3_out));
  Multiplexer #(.width(16)) multiplexer_2 (.in0(Datain), .in1(ALU), .out(multiplexer_2_out), .sel(ALUOE));
  Register #(.width(16)) R_2 (.D(Datain), .en(decoder_1_out3), .clk(CLK), .Q(R_2_q), .clr(multiplexer_3_out));
  Register #(.width(16)) R_3 (.D(Datain), .en(decoder_1_out4), .clk(CLK), .Q(R_3_q), .clr(multiplexer_3_out));
  Register #(.width(16)) R_4 (.D(Datain), .en(decoder_1_out5), .clk(CLK), .Q(R_4_q), .clr(multiplexer_3_out));
  Register #(.width(16)) R_5 (.D(Datain), .en(decoder_1_out6), .clk(CLK), .Q(R_5_q), .clr(multiplexer_3_out));
  Register #(.width(16)) R_6 (.D(Datain), .en(decoder_1_out7), .clk(CLK), .Q(R_6_q), .clr(multiplexer_3_out));
  Register #(.width(16)) R_7 (.D(Datain), .en(decoder_1_out8), .clk(CLK), .Q(R_7_q), .clr(multiplexer_3_out));
  Register #(.width(16)) R_8 (.D(Datain), .en(decoder_1_out9), .clk(CLK), .Q(R_8_q), .clr(multiplexer_3_out));
  Register #(.width(16)) R_9 (.D(Datain), .en(decoder_1_out10), .clk(CLK), .Q(R_9_q), .clr(multiplexer_3_out));
  Register #(.width(16)) RAMADDR (.D(Datain), .en(decoder_1_out11), .clk(CLK), .Q(RAMADDROUT), .clr(multiplexer_3_out));
  Register #(.width(16)) REGADDR (.D(Datain), .en(decoder_1_out12), .clk(CLK), .Q(ADDR), .clr(multiplexer_3_out));
  assign Output_bus_1 = decoder_2_out0 ? ACCOUT : 16'bz;  // Controlled_Buffer controlled_buffer_1
  assign Output_bus_1 = decoder_2_out1 ? REG0 : 16'bz;  // Controlled_Buffer controlled_buffer_2
  assign Output_bus_1 = decoder_2_out2 ? REG1 : 16'bz;  // Controlled_Buffer controlled_buffer_3
  assign Output_bus_1 = decoder_2_out3 ? R_2_q : 16'bz;  // Controlled_Buffer controlled_buffer_4
  assign Output_bus_1 = decoder_2_out4 ? R_3_q : 16'bz;  // Controlled_Buffer controlled_buffer_5
  assign Output_bus_1 = decoder_2_out5 ? R_4_q : 16'bz;  // Controlled_Buffer controlled_buffer_6
  assign Output_bus_1 = decoder_2_out6 ? R_5_q : 16'bz;  // Controlled_Buffer controlled_buffer_7
  assign Output_bus_1 = decoder_2_out7 ? R_6_q : 16'bz;  // Controlled_Buffer controlled_buffer_8
  assign Output_bus_1 = decoder_2_out8 ? R_7_q : 16'bz;  // Controlled_Buffer controlled_buffer_9
  assign Output_bus_1 = decoder_2_out9 ? R_8_q : 16'bz;  // Controlled_Buffer controlled_buffer_10
  assign Output_bus_1 = decoder_2_out10 ? R_9_q : 16'bz;  // Controlled_Buffer controlled_buffer_11
  assign Output_bus_1 = decoder_2_out11 ? RAMADDROUT : 16'bz;  // Controlled_Buffer controlled_buffer_12
  assign Output_bus_1 = decoder_2_out12 ? ADDR : 16'bz;  // Controlled_Buffer controlled_buffer_13
  Decoder #(.select(4)) decoder_2 (
    .out0(decoder_2_out0), .out1(decoder_2_out1), .out2(decoder_2_out2), .out3(decoder_2_out3),
    .out4(decoder_2_out4), .out5(decoder_2_out5), .out6(decoder_2_out6), .out7(decoder_2_out7),
    .out8(decoder_2_out8), .out9(decoder_2_out9), .out10(decoder_2_out10), .out11(decoder_2_out11),
    .out12(decoder_2_out12), .out13(BUSREQ), .out14(RAMOE), .out15(IMM), .sel(REGOUTSEL), .en(Enable));
  or or_1 (REGOUT, decoder_2_out0, decoder_2_out1, decoder_2_out2, decoder_2_out3, decoder_2_out4, decoder_2_out5, decoder_2_out6, decoder_2_out7, decoder_2_out8, decoder_2_out9, decoder_2_out10, decoder_2_out11, decoder_2_out12);
  Multiplexer multiplexer_3 (.in0(1'b0), .in1(t_ff_1_qn), .out(multiplexer_3_out), .sel(t_ff_1_qn));
  Multiplexer multiplexer_4 (.in0(decoder_1_out14), .in1(multiplexer_3_out), .out(RAMWE), .sel(multiplexer_3_out));
  T_Flip_Flop t_ff_1 (.T(or_2_out), .clk(CLK), .Qn(t_ff_1_qn));  // open: Q, reset, preset
  or or_2 (or_2_out, t_ff_1_qn, RESET);
endmodule

module ALU16 (
  input  [2:0] MUX,
  input  [15:0] REG3,
  input  [15:0] ACC,
  input  [1:0] COMPAREINST,
  input  BRANCHOE,
  input  [15:0] REG1,
  output [15:0] ALUOUT,
  output Output_1
);

  wire adder_1_cout, CFLAG_q, comparator_1_eq, comparator_1_gt, not_1_out, or_2_out, subtractor_1_bout,
       undriven, undriven_2, undriven_3;
  wire [15:0] adder_1_out, and_1_out, divider_1_out, divider_1_rem, multiplier_1_cout, multiplier_1_out,
       not_2_out, or_1_out, subtractor_1_out, xor_1_out;

  Comparator #(.mode("unsigned"), .width(16)) comparator_1 (
    .a(REG1), .b({16{1'b0}}), .gt(comparator_1_gt), .eq(comparator_1_eq));  // open: lt
  Adder #(.width(16)) adder_1 (.a(ACC), .b(REG3), .out(adder_1_out), .cout(adder_1_cout));  // open: cin
  Subtractor #(.width(16)) subtractor_1 (
    .a(ACC), .b(REG3), .out(subtractor_1_out), .bout(subtractor_1_bout));  // open: bin
  Multiplier #(.width(16)) multiplier_1 (
    .a(ACC), .b(REG3), .out(multiplier_1_out), .cout(multiplier_1_cout));  // open: cin
  Divider #(.width(16)) divider_1 (.a(ACC), .b(REG3), .out(divider_1_out), .rem(divider_1_rem));  // open: upper
  not not_1 (not_1_out, comparator_1_eq);
  assign xor_1_out = ACC ^ REG3;  // XOR_Gate xor_1, 16 bits wide
  Multiplexer #(.enable("true"), .select(2)) multiplexer_1 (
    .in0(1'b1), .in1(comparator_1_gt), .in2(not_1_out), .in3(comparator_1_eq), .out(Output_1),
    .sel(COMPAREINST), .en(BRANCHOE));
  assign and_1_out = ACC & REG3;  // AND_Gate and_1, 16 bits wide
  assign or_1_out = ACC | REG3;  // OR_Gate or_1, 16 bits wide
  assign not_2_out = ~ACC;  // NOT_Gate not_2, 16 bits wide
  or or_2 (or_2_out, adder_1_cout, subtractor_1_bout);
  Comparator #(.width(16)) comparator_2 (.a(REG3), .b(ACC));  // open: gt, eq, lt
  Register #(.width(1)) CFLAG (.D(or_2_out), .en(undriven_2), .clk(undriven_3), .Q(CFLAG_q));  // open: clr
  Multiplexer #(.select(3), .width(16)) multiplexer_2 (
    .in0(adder_1_out), .in1(subtractor_1_out), .in2(multiplier_1_out), .in3(divider_1_out), .in4(xor_1_out),
    .in5(and_1_out), .in6(or_1_out), .in7(not_2_out), .out(ALUOUT), .sel(MUX));
  Register #(.width(1)) ZFLAG (.en(undriven), .clk(undriven_3));  // open: D, Q, clr
endmodule

module GPU (
  input  [15:0] S,
  input  W,
  input  [15:0] ADDR,
  input  [15:0] PROGRAM,
  input  [15:0] DATA,
  input  R,
  input  clk,
  output [4:0] X,
  output [4:0] Y,
  output [23:0] RGBOUT,
  output WRITE
);

  wire and_1_out, comparator_1_eq, comparator_2_eq, comparator_3_eq, or_1_out, or_2_out, t_ff_1_qn;
  wire [5:0] or_4_out;
  wire [7:0] rgb_1_b, rgb_1_g, rgb_1_r;
  wire [15:0] and_4_out, and_5_out, or_3_out;
  wire [15:15] and_2_out, and_3_out;

  and and_1 (and_1_out, W, comparator_1_eq);
  Comparator #(.width(16)) comparator_1 (.a(S), .b({16{1'b0}}), .eq(comparator_1_eq));  // open: gt, lt
  Comparator #(.width(16)) comparator_2 (.a(ADDR), .b(16'h1), .eq(comparator_2_eq));  // open: gt, lt
  and and_2 (and_2_out[15], comparator_2_eq, and_1_out);
  Comparator #(.width(16)) comparator_3 (.a(ADDR), .b(16'h1), .eq(comparator_3_eq));  // open: gt, lt
  and and_3 (and_3_out[15], comparator_3_eq, and_1_out);
  or or_1 (or_1_out, and_3_out[15], R);
  or or_2 (or_2_out, or_1_out, and_1_out);
  assign and_4_out = {16{and_2_out[15]}} & DATA;  // AND_Gate and_4, 16 bits wide
  assign and_5_out = {16{and_3_out[15]}} & DATA;  // AND_Gate and_5, 16 bits wide
  assign or_3_out = PROGRAM | and_4_out;  // OR_Gate or_3, 16 bits wide
  assign or_4_out = or_3_out[15:10] | and_5_out[15:10];  // OR_Gate or_4, 6 bits wide
  RGB rgb_1 (.REDGRNBLU(or_4_out), .B(rgb_1_b), .G(rgb_1_g), .R(rgb_1_r));
  Register #(.width(5)) register_1 (.D(or_3_out[4:0]), .en(or_2_out), .clk(clk), .Q(X), .clr(t_ff_1_qn));
  Register #(.width(5)) register_2 (.D(or_3_out[9:5]), .en(or_2_out), .clk(clk), .Q(Y), .clr(t_ff_1_qn));
  Register #(.width(24)) register_3 (
    .D({rgb_1_r, rgb_1_g, rgb_1_b}), .en(or_2_out), .clk(clk), .Q(RGBOUT), .clr(t_ff_1_qn));
  Register #(.width(1)) register_4 (.D(or_1_out), .en(or_2_out), .clk(clk), .Q(WRITE), .clr(t_ff_1_qn));
  T_Flip_Flop t_ff_1 (.T(t_ff_1_qn), .clk(clk), .Qn(t_ff_1_qn));  // open: Q, reset, preset
endmodule

module RGB (
  input  [5:0] REDGRNBLU,
  output [7:0] B,
  output [7:0] G,
  output [7:0] R
);


  assign B = {REDGRNBLU[1:0], REDGRNBLU[1:0], REDGRNBLU[1:0], REDGRNBLU[1:0]};
  assign G = {REDGRNBLU[3:2], REDGRNBLU[3:2], REDGRNBLU[3:2], REDGRNBLU[3:2]};
  assign R = {REDGRNBLU[5:4], REDGRNBLU[5:4], REDGRNBLU[5:4], REDGRNBLU[5:4]};
endmodule

module Stack (
  input  StackOE,
  input  [1:0] StackINST,
  input  clk,
  input  RESET,
  input  [15:0] STACKIN,
  output POP,
  output [15:0] STACKOUT,
  output [3:0] POINTER
);

  wire comparator_1_eq, counter_1_carry, decoder_1_out0, decoder_1_out1, decoder_1_out2, decoder_1_out3,
       multiplexer_1_out, multiplexer_2_out, multiplexer_5_out, or_1_out, s_r_ff_1_q;
  wire [3:0] counter_2_q, multiplexer_3_out, multiplexer_4_out, subtractor_1_out, subtractor_2_out;

  Decoder #(.select(2)) decoder_1 (
    .out0(decoder_1_out0), .out1(decoder_1_out1), .out2(decoder_1_out2), .out3(decoder_1_out3),
    .sel(StackINST), .en(StackOE));
  Multiplexer multiplexer_1 (.in0(StackOE), .in1(1'b0), .out(multiplexer_1_out), .sel(decoder_1_out3));
  or or_1 (or_1_out, decoder_1_out0, decoder_1_out2);
  Counter #(.max('hf), .ongoal("stay"), .width(4)) counter_1 (
    .load(multiplexer_5_out), .D(multiplexer_4_out), .count(multiplexer_1_out), .Q(POINTER),
    .carry(counter_1_carry), .up(or_1_out), .clk(clk), .clr(RESET));
  or or_2 (POP, decoder_1_out1, decoder_1_out3);
  Counter #(.max('hf), .ongoal("stay"), .width(4)) counter_2 (
    .count(or_1_out), .Q(counter_2_q), .clk(clk), .clr(multiplexer_2_out));  // open: load, D, carry, up
  Multiplexer multiplexer_2 (.in0(RESET), .in1(counter_1_carry), .out(multiplexer_2_out), .sel(counter_1_carry));
  Multiplexer #(.width(4)) multiplexer_3 (
    .in0(POINTER), .in1(subtractor_1_out), .out(multiplexer_3_out), .sel(multiplexer_5_out));
  Subtractor #(.width(4)) subtractor_1 (.a(counter_2_q), .b(4'b0001), .out(subtractor_1_out));  // open: bin, bout
  S_R_Flip_Flop s_r_ff_1 (.S(or_1_out), .R(POP), .clk(clk), .Q(s_r_ff_1_q), .reset(RESET));  // open: Qn, preset
  Subtractor #(.width(4)) subtractor_2 (.a(subtractor_1_out), .b(4'b0001), .out(subtractor_2_out));  // open: bin, bout
  Multiplexer #(.width(4)) multiplexer_4 (
    .in0(subtractor_2_out), .in1(4'b0000), .out(multiplexer_4_out), .sel(comparator_1_eq));
  Comparator #(.mode("unsigned"), .width(4)) comparator_1 (
    .a(subtractor_2_out), .b(4'b1111), .eq(comparator_1_eq));  // open: gt, lt
  STACKREG STACKREG_1 (
    .STACKIN(STACKIN), .clk(clk), .SP(multiplexer_3_out), .StackCE(or_1_out), .POP(POP), .RESET(RESET),
    .STACKOUT(STACKOUT));
  Multiplexer multiplexer_5 (.in0(1'b0), .in1(s_r_ff_1_q), .out(multiplexer_5_out), .sel(POP));
endmodule

module MMU (
  input  [15:0] ADDR,
  input  [15:0] DATA,
  input  clk,
  input  Reset,
  output [15:0] MEMADDR
);

  wire comparator_1_eq;

  Comparator #(.width(16)) comparator_1 (.a({16{1'b1}}), .b(ADDR), .eq(comparator_1_eq));  // open: gt, lt
  Register #(.width(16)) register_1 (.D(DATA), .en(comparator_1_eq), .clk(clk), .Q(MEMADDR), .clr(Reset));
endmodule

module BANK (
  input  [15:0] PC,
  input  [15:0] ADDR,
  output [31:0] out_3
);

  wire comparator_1_eq, comparator_1_gt, comparator_1_lt, or_1_out;
  wire [31:0] ROM0_data, ROM1_data;

  Comparator #(.mode("unsigned"), .width(16)) comparator_1 (
    .a(ADDR), .b(16'h8000), .gt(comparator_1_gt), .eq(comparator_1_eq), .lt(comparator_1_lt));
  ROM #(.addrWidth(16), .dataWidth(32)) ROM0 (.addr(PC), .data(ROM0_data));
  ROM #(.addrWidth(16), .dataWidth(32)) ROM1 (.addr(PC), .data(ROM1_data));
  or or_1 (or_1_out, comparator_1_eq, comparator_1_gt);
  assign out_3 = 1'b1 ? ROM0_data : 32'bz;  // Controlled_Buffer controlled_buffer_1

  // Notes on the sheet:
  //   contents of ROM0 (hex, n*v repeats v):
  //   0 0 80cfffff 800d0000 801f0007 c0000000 80020000 20000000 80cf002d 40000000 80cfffff 800d0000
  //   801f0007 c0000000 80020000 20000000 80cf001b 40000000 80cfffff 800d0000 801f0007 c0000000 80020000
  //   20000000 80cf0064 40000000 60000000 80cffffe 801f000a 800d0000 c1000000 80cf0027 43000000 80200000
  //   80cf0025 43000000 80300000 80cf001b 40000000 80cf0000 80df0007 80cffffe 21000000 80c20000 40000000
  //   80cf0000 80df0043 80df0048 80df004f 80df004f 80df0053 80df0045 80df0020 80df0059 80df004f 80df0055
  //   80df0052 80df0020 80df0054 80df0045 80df0053 80df0054 80df000a 80df0031 80df003a 80df0020 80df0052
  //   80df0041 80df004d 80df000a 80df0032 80df003a 80df0020 80df0049 80df004f 80df000a 80df0033 80df003a
  //   80df0020 80df0052 80df0045 80df0047 80df0049 80df0053 80df0054 80df0045 80df0052 80df0053 80df000a
  //   80df0034 80df003a 80df0020 80df0053 80df0054 80df0041 80df0043 80df004b 21000000 80c20000 40000000
  //   80030000 801f0031 c1000000 80cf0075 43000000 801f0032 c1000000 80cf0097 43000000 801f0033 c1000000
  //   80cf009a 43000000 801f0034 c1000000 80cf009d 43000000 80bf0000 80ef0048 80bf0001 80ef0045 80bf0002
  //   80ef004c 80bf0003 80ef004c 80bf0004 80ef004f 80cf0000 80bf0000 800e0000 800e0000 80d00000 80bf0001
  //   800e0000 800e0000 80d00000 80bf0002 800e0000 800e0000 80d00000 80bf0003 800e0000 800e0000 80d00000
  //   80bf0004 800e0000 800e0000 80d00000 21000000 80c20000 40000000 21000000 80c20000 40000000 21000000
  //   80c20000 40000000 800f004f 20000000 800f004c 20000000 800f004c 20000000 800f0045 20000000 800f0048
  //   20000000 80cf0000 21000000 80d20000 21000000 80d20000 21000000 80d20000 21000000 80d20000 21000000
  //   80d20000 21000000 80c20000 40000000
  //   contents of ROM1 (hex, n*v repeats v):
  //   0 0 80cf0000 80df0048 80df0045 80df004c 80df004c 80df004f 80cfffff 800d0000 801f0004 c0000000
  //   80020000 20000000 80cf001f 40000000 80df0054 80df0045 80df0053 80df0054 80df0020 80df0033 80cf0029
  //   40000000 80cf0000 80df0054 80df0045 80df0053 80df0054 80df0020 80df0031 80cf0000 80df0020 80df0057
  //   80df004f 80df0052 80df004c 80df0044 21000000 80c20000 40000000 80cf0000 80df0054 80df0045 80df0053
  //   80df0054 80df0020 80df0032
endmodule

module BCDTO7SEG (
  input  [15:0] DATAIN,
  input  ENA,
  input  CLK,
  input  [15:0] in_4,
  output [3:0] out_5,
  output [3:0] out_6,
  output [3:0] out_7,
  output [3:0] out_8,
  output [3:0] out_9,
  output [3:0] out_10
);

  wire comparator_1_eq, multiplexer_1_out;
  wire [15:0] register_1_q;

  Register #(.width(16)) register_1 (.D(DATAIN), .en(multiplexer_1_out), .clk(CLK), .Q(register_1_q));  // open: clr
  Multiplexer multiplexer_1 (.in0(1'b0), .in1(ENA), .out(multiplexer_1_out), .sel(comparator_1_eq));
  Comparator #(.mode("unsigned"), .width(16)) comparator_1 (.a(in_4), .b(16'h3), .eq(comparator_1_eq));  // open: gt, lt
  // Binary_to_BCD_converter #(.binvalue(8)) binary_to_bcd_converter_1: pin names not known; wires that end beside it: out_5, out_6, out_7
  // Binary_to_BCD_converter #(.binvalue(8)) binary_to_bcd_converter_2: pin names not known; wires that end beside it: out_8, out_9, out_10
endmodule

module STACKREG (
  input  [15:0] STACKIN,
  input  clk,
  input  [3:0] SP,
  input  StackCE,
  input  POP,
  input  RESET,
  output [15:0] STACKOUT
);

  wire decoder_1_out0, decoder_1_out1, decoder_1_out2, decoder_1_out3, decoder_1_out4, decoder_1_out5,
       decoder_1_out6, decoder_1_out7, decoder_1_out8, decoder_1_out9, decoder_1_out10, decoder_1_out11,
       decoder_1_out12, decoder_1_out13, decoder_1_out14, decoder_1_out15;
  wire [15:0] register_1_q, register_2_q, register_3_q, register_4_q, register_5_q, register_6_q,
       register_7_q, register_8_q, register_9_q, register_10_q, register_11_q, register_12_q, register_13_q,
       register_14_q, register_15_q, register_16_q;

  Decoder #(.select(4)) decoder_1 (
    .out0(decoder_1_out0), .out1(decoder_1_out1), .out2(decoder_1_out2), .out3(decoder_1_out3),
    .out4(decoder_1_out4), .out5(decoder_1_out5), .out6(decoder_1_out6), .out7(decoder_1_out7),
    .out8(decoder_1_out8), .out9(decoder_1_out9), .out10(decoder_1_out10), .out11(decoder_1_out11),
    .out12(decoder_1_out12), .out13(decoder_1_out13), .out14(decoder_1_out14), .out15(decoder_1_out15),
    .sel(SP), .en(StackCE));
  Register #(.width(16)) register_1 (.D(STACKIN), .en(decoder_1_out0), .clk(clk), .Q(register_1_q), .clr(RESET));
  Register #(.width(16)) register_2 (.D(STACKIN), .en(decoder_1_out1), .clk(clk), .Q(register_2_q), .clr(RESET));
  Register #(.width(16)) register_3 (.D(STACKIN), .en(decoder_1_out2), .clk(clk), .Q(register_3_q), .clr(RESET));
  Register #(.width(16)) register_4 (.D(STACKIN), .en(decoder_1_out3), .clk(clk), .Q(register_4_q), .clr(RESET));
  Register #(.width(16)) register_5 (.D(STACKIN), .en(decoder_1_out4), .clk(clk), .Q(register_5_q), .clr(RESET));
  Register #(.width(16)) register_6 (.D(STACKIN), .en(decoder_1_out5), .clk(clk), .Q(register_6_q), .clr(RESET));
  Register #(.width(16)) register_7 (.D(STACKIN), .en(decoder_1_out6), .clk(clk), .Q(register_7_q), .clr(RESET));
  Register #(.width(16)) register_8 (.D(STACKIN), .en(decoder_1_out7), .clk(clk), .Q(register_8_q), .clr(RESET));
  Register #(.width(16)) register_9 (.D(STACKIN), .en(decoder_1_out8), .clk(clk), .Q(register_9_q), .clr(RESET));
  Register #(.width(16)) register_10 (.D(STACKIN), .en(decoder_1_out9), .clk(clk), .Q(register_10_q), .clr(RESET));
  Register #(.width(16)) register_11 (.D(STACKIN), .en(decoder_1_out10), .clk(clk), .Q(register_11_q), .clr(RESET));
  Register #(.width(16)) register_12 (.D(STACKIN), .en(decoder_1_out11), .clk(clk), .Q(register_12_q), .clr(RESET));
  Register #(.width(16)) register_13 (.D(STACKIN), .en(decoder_1_out12), .clk(clk), .Q(register_13_q), .clr(RESET));
  Register #(.width(16)) register_14 (.D(STACKIN), .en(decoder_1_out13), .clk(clk), .Q(register_14_q), .clr(RESET));
  Register #(.width(16)) register_15 (.D(STACKIN), .en(decoder_1_out14), .clk(clk), .Q(register_15_q), .clr(RESET));
  Register #(.width(16)) register_16 (.D(STACKIN), .en(decoder_1_out15), .clk(clk), .Q(register_16_q), .clr(RESET));
  Multiplexer #(.enable("true"), .select(4), .width(16)) multiplexer_1 (
    .in0(register_1_q), .in1(register_2_q), .in2(register_3_q), .in3(register_4_q), .in4(register_5_q),
    .in5(register_6_q), .in6(register_7_q), .in7(register_8_q), .in8(register_9_q), .in9(register_10_q),
    .in10(register_11_q), .in11(register_12_q), .in12(register_13_q), .in13(register_14_q),
    .in14(register_15_q), .in15(register_16_q), .out(STACKOUT), .sel(SP), .en(POP));
endmodule

module Multicore (
);

  wire multiplexer_1_out, Slave_p2;
  wire [15:0] undriven;

  Multiplexer multiplexer_1 (.out(multiplexer_1_out));  // open: in0, in1, sel
  CPU Master (
    .DATAIN(undriven), .clk(Slave_p2));  // open: ROMIN, RAMOUT, Reset, RW, ROMADDR, RAMIN, RAMADDR, RAMWE, RAMOE, Dataout, ADDR, BUSREQ, BUSWRITE, HLT, POINTER
  // CPU Slave: pin names not known; wires that end beside it: multiplexer_1_out, Slave_p2
  RAM #(.addrWidth(16), .dataWidth(16)) Cache ();  // open: addr, we, oe, clk, din, dout
endmodule

module GPUmkII (
  input  RD,
  input  WR,
  input  [15:0] DATA,
  input  clk,
  output WE,
  output [3:0] CLR,
  output [7:0] x,
  output [7:0] y,
  output OUTCLK
);

  wire and_1_out, and_2_out, bootstrap_1_cpuclk, controlled_buffer_3_out, counter_1_carry, counter_2_carry,
       cpu_1_busreq, cpu_1_buswrite, cpu_1_ramoe, cpu_1_ramwe, d_ff_1_q, demultiplexer_1_out0,
       demultiplexer_1_out1, demultiplexer_2_out0, demultiplexer_2_out1, not_2_out, or_1_out, or_2_out,
       or_3_out, t_ff_1_q;
  wire [7:0] controlled_buffer_1_out, controlled_buffer_2_out;
  wire [9:0] counter_1_q, counter_2_q;
  wire [15:0] cpu_1_addr, cpu_1_dataout, cpu_1_ramaddr, cpu_1_romaddr, ram_1_dout, ram_2_dout;
  wire [31:0] bootstrap_1_dataout;

  BOOTSTRAP bootstrap_1 (
    .WE(cpu_1_buswrite), .clk(clk), .DATA(cpu_1_dataout), .ADDR(cpu_1_addr), .CPUADDR(cpu_1_romaddr),
    .cpuclk(bootstrap_1_cpuclk), .DATAOUT(bootstrap_1_dataout));
  Counter #(.max('h3ff), .width(10)) counter_1 (
    .Q(counter_1_q), .carry(counter_1_carry), .clk(OUTCLK));  // open: load, D, count, up, clr
  not not_1 (OUTCLK, clk);
  CPU cpu_1 (
    .DATAIN(DATA), .clk(bootstrap_1_cpuclk), .ROMIN(bootstrap_1_dataout), .ROMADDR(cpu_1_romaddr),
    .RAMADDR(cpu_1_ramaddr), .RAMWE(cpu_1_ramwe), .RAMOE(cpu_1_ramoe), .Dataout(cpu_1_dataout),
    .ADDR(cpu_1_addr), .BUSREQ(cpu_1_busreq), .BUSWRITE(cpu_1_buswrite));  // open: RAMOUT, Reset, RW, RAMIN, HLT, POINTER
  Counter #(.max('h3ff), .width(10)) counter_2 (
    .count(counter_1_carry), .Q(counter_2_q), .carry(counter_2_carry), .clk(OUTCLK));  // open: load, D, up, clr
  and and_1 (and_1_out, counter_1_carry, counter_2_carry);
  assign controlled_buffer_1_out = or_1_out ? counter_1_q[7:0] : 8'bz;  // Controlled_Buffer controlled_buffer_1
  or or_1 (or_1_out, ~counter_1_q[8], ~counter_1_q[9]);  // OR_Gate
  assign controlled_buffer_2_out = or_2_out ? counter_2_q[7:0] : 8'bz;  // Controlled_Buffer controlled_buffer_2
  Pull_Resistor pull_resistor_1 (.node(controlled_buffer_2_out));
  or or_2 (or_2_out, ~counter_2_q[8], ~counter_2_q[9]);  // OR_Gate
  T_Flip_Flop t_ff_1 (.T(and_1_out), .clk(OUTCLK), .Q(t_ff_1_q));  // open: Qn, reset, preset
  Pull_Resistor pull_resistor_2 (.node(controlled_buffer_1_out));
  assign controlled_buffer_3_out = OUTCLK ? t_ff_1_q : 1'bz;  // Controlled_Buffer controlled_buffer_3
  assign controlled_buffer_3_out = not_2_out ? ~t_ff_1_q : 1'bz;  // Controlled_Inverter controlled_inverter_1
  not not_2 (not_2_out, OUTCLK);
  or or_3 (or_3_out, OUTCLK, cpu_1_ramoe);
  Demultiplexer demultiplexer_1 (
    .out0(demultiplexer_1_out0), .out1(demultiplexer_1_out1), .in(cpu_1_ramwe), .sel(controlled_buffer_3_out));
  Demultiplexer demultiplexer_2 (
    .out0(demultiplexer_2_out0), .out1(demultiplexer_2_out1), .in(or_3_out), .sel(controlled_buffer_3_out));
  RAM #(.addrWidth(16), .dataWidth(16)) ram_1 (
    .addr(cpu_1_ramaddr), .we(demultiplexer_1_out0), .oe(demultiplexer_2_out0), .clk(OUTCLK),
    .din(cpu_1_dataout), .dout(ram_1_dout));
  RAM #(.addrWidth(16), .dataWidth(16)) ram_2 (
    .addr(cpu_1_ramaddr), .we(demultiplexer_1_out1), .oe(demultiplexer_2_out1), .clk(not_2_out),
    .din(cpu_1_dataout), .dout(ram_2_dout));
  GPUROM gpurom_1 (
    .RD(cpu_1_busreq), .WR(cpu_1_buswrite), .DATA(cpu_1_dataout), .clk(OUTCLK), .XOUT(x), .YOUT(y),
    .WROUT(WE), .CLR(CLR));  // open: ADDR
  and and_2 (and_2_out, OUTCLK, controlled_buffer_3_out);
  Multiplexer #(.enable("true"), .width(16)) multiplexer_1 (
    .in0(ram_1_dout), .in1(ram_2_dout), .sel(controlled_buffer_3_out), .en(d_ff_1_q));  // open: out
  D_Flip_Flop d_ff_1 (.D(and_2_out), .clk(OUTCLK), .Q(d_ff_1_q));  // open: Qn, preset, reset
endmodule

module AltairClone (
);

  wire altairram_1_p1, altairram_1_p2, altairram_1_p3, altairram_1_p4, altairram_1_p5, altairram_1_p6,
       altairram_1_p10, clock_1_out, cpu_1_p5, cpu_1_p9, cpu_1_p10, cpu_1_p13, cpu_1_p14, cpu_1_p15,
       DATABUS_p1, INST_p1, PC_p1, SP_p1;
  wire [15:0] ADDR_p1, cpu_1_p7, cpu_1_p8, dipswitch_1_sw16, dipswitch_2_sw16;

  Clock clock_1 (.out(clock_1_out));
  DipSwitch #(.number(16)) dipswitch_1 (
    .sw1(dipswitch_1_sw16[15]), .sw2(dipswitch_1_sw16[14]), .sw3(dipswitch_1_sw16[13]),
    .sw4(dipswitch_1_sw16[12]), .sw5(dipswitch_1_sw16[11]), .sw6(dipswitch_1_sw16[10]),
    .sw7(dipswitch_1_sw16[9]), .sw8(dipswitch_1_sw16[8]), .sw9(dipswitch_1_sw16[7]),
    .sw10(dipswitch_1_sw16[6]), .sw11(dipswitch_1_sw16[5]), .sw12(dipswitch_1_sw16[4]),
    .sw13(dipswitch_1_sw16[3]), .sw14(dipswitch_1_sw16[2]), .sw15(dipswitch_1_sw16[1]),
    .sw16(dipswitch_1_sw16[0]));
  // LedBar #(.inputtype("row"), .matrixcols(4)) SP: pin names not known; wires that end beside it: SP_p1
  // LedBar #(.inputtype("row"), .matrixcols(32)) INST: pin names not known; wires that end beside it: INST_p1
  // LedBar #(.inputtype("row"), .matrixcols(16)) PC: pin names not known; wires that end beside it: PC_p1
  DipSwitch #(.number(16)) dipswitch_2 (
    .sw1(dipswitch_2_sw16[15]), .sw2(dipswitch_2_sw16[14]), .sw3(dipswitch_2_sw16[13]),
    .sw4(dipswitch_2_sw16[12]), .sw5(dipswitch_2_sw16[11]), .sw6(dipswitch_2_sw16[10]),
    .sw7(dipswitch_2_sw16[9]), .sw8(dipswitch_2_sw16[8]), .sw9(dipswitch_2_sw16[7]),
    .sw10(dipswitch_2_sw16[6]), .sw11(dipswitch_2_sw16[5]), .sw12(dipswitch_2_sw16[4]),
    .sw13(dipswitch_2_sw16[3]), .sw14(dipswitch_2_sw16[2]), .sw15(dipswitch_2_sw16[1]),
    .sw16(dipswitch_2_sw16[0]));
  LedBar #(.matrixcols(4)) ledbar_1 (.led0(cpu_1_p14), .led1(cpu_1_p13), .led2(cpu_1_p5), .led3(cpu_1_p15));
  // ALTAIRRAM altairram_1: pin names not known; wires that end beside it: altairram_1_p1, altairram_1_p2, altairram_1_p3, altairram_1_p4, altairram_1_p5, altairram_1_p6, clock_1_out, {dipswitch_1_sw16, dipswitch_2_sw16}, altairram_1_p5, altairram_1_p10, INST_p1, PC_p1, PC_p1
  Button STEP (.out(altairram_1_p5));
  DipSwitch #(.number(2)) dipswitch_3 (.sw1(altairram_1_p1), .sw2(altairram_1_p5));
  // LedBar #(.inputtype("row"), .matrixcols(16)) DATABUS: pin names not known; wires that end beside it: DATABUS_p1
  // LedBar #(.inputtype("row"), .matrixcols(16)) ADDR: pin names not known; wires that end beside it: ADDR_p1
  Button STR (.out(altairram_1_p6));
  Button CLR (.out(altairram_1_p3));
  // CPU cpu_1: pin names not known; wires that end beside it: altairram_1_p10, INST_p1, ADDR_p1, altairram_1_p3, cpu_1_p5, altairram_1_p2, cpu_1_p7, cpu_1_p8, cpu_1_p9, cpu_1_p10, DATABUS_p1, ADDR_p1, cpu_1_p13, cpu_1_p14, cpu_1_p15, SP_p1
  Button JMP (.out(altairram_1_p4));
  RAM #(.addrWidth(16), .asyncread("true"), .dataWidth(16), .\type ("nonvolatile")) ram_1 (
    .addr(cpu_1_p8), .we(cpu_1_p9), .oe(cpu_1_p10), .clk(clock_1_out), .din(cpu_1_p7), .dout(ADDR_p1));

  // Notes on the sheet:
  //   RUN/STEP PROGRAM
endmodule

module ALTAIRRAM (
  input  RUN,
  input  [15:0] CPU,
  input  clr,
  input  JMP,
  input  STEP,
  input  STR,
  input  CLK,
  input  [31:0] DATA,
  input  STEPENABLE,
  output [15:0] GPIO,
  output out_11,
  output [31:0] out_12,
  output [15:0] PC
);

  wire demultiplexer_1_out0, demultiplexer_1_out1, multiplexer_1_out, multiplexer_3_out;
  wire [15:0] counter_1_q;

  Multiplexer multiplexer_1 (.in0(STEP), .in1(JMP), .out(multiplexer_1_out), .sel(JMP));
  Counter #(.max('hffff), .width(16)) counter_1 (
    .load(JMP), .D(DATA[31:16]), .Q(counter_1_q), .clk(multiplexer_1_out), .clr(clr));  // open: count, carry, up
  Demultiplexer demultiplexer_1 (.out0(demultiplexer_1_out0), .out1(demultiplexer_1_out1), .in(1'b1), .sel(STR));
  RAM #(.addrWidth(16), .asyncread("true"), .clearpin("true"), .dataWidth(32)) ram_1 (
    .addr(PC), .we(demultiplexer_1_out1), .oe(demultiplexer_1_out0), .clk(CLK), .din(DATA), .dout(out_12),
    .clr(clr));
  Multiplexer #(.width(16)) multiplexer_2 (.in0(counter_1_q), .in1(CPU), .out(PC), .sel(RUN));
  Multiplexer multiplexer_3 (.in0(1'b0), .in1(CLK), .out(multiplexer_3_out), .sel(RUN));
  Multiplexer multiplexer_4 (.in0(multiplexer_3_out), .in1(STEP), .out(out_11), .sel(STEPENABLE));
endmodule

module BOOTSTRAP (
  input  WE,
  input  clk,
  input  [15:0] DATA,
  input  [15:0] ADDR,
  input  [15:0] CPUADDR,
  output cpuclk,
  output [31:0] DATAOUT
);

  wire and_1_out, and_2_out, and_3_out, and_4_out, comparator_1_eq, controlled_buffer_1_out, d_ff_1_q,
       multiplexer_1_out, t_ff_1_q, t_ff_2_qn;
  wire [15:0] HIGH_dout, LOW_dout;
  wire [31:0] rom_1_data;

  and and_1 (and_1_out, t_ff_1_q, clk);
  assign controlled_buffer_1_out = comparator_1_eq ? WE : 1'bz;  // Controlled_Buffer controlled_buffer_1
  Comparator #(.mode("unsigned"), .width(16)) comparator_1 (
    .a(ADDR), .b(16'hfe), .eq(comparator_1_eq));  // open: gt, lt
  Pull_Resistor pull_resistor_1 (.node(controlled_buffer_1_out));
  T_Flip_Flop t_ff_1 (.T(and_4_out), .clk(clk), .Q(t_ff_1_q));  // open: Qn, reset, preset
  and and_2 (and_2_out, CPUADDR[0], CPUADDR[1], CPUADDR[2], CPUADDR[3], CPUADDR[4], CPUADDR[5], CPUADDR[6], CPUADDR[7], CPUADDR[9], CPUADDR[10], CPUADDR[11], CPUADDR[12], CPUADDR[13], CPUADDR[14], CPUADDR[15], CPUADDR[8]);
  and and_3 (and_3_out, DATA[0], DATA[1], DATA[2], DATA[3], DATA[4], DATA[5], DATA[6], DATA[7], DATA[9], DATA[10], DATA[11], DATA[12], DATA[13], DATA[14], DATA[15], DATA[8]);
  ROM #(.addrWidth(16), .dataWidth(32)) rom_1 (.addr(ADDR), .data(rom_1_data));
  and and_4 (and_4_out, and_3_out, and_2_out);
  T_Flip_Flop t_ff_2 (.T(t_ff_2_qn), .clk(clk), .Qn(t_ff_2_qn));  // open: Q, reset, preset
  Multiplexer multiplexer_1 (.in0(and_1_out), .in1(t_ff_2_qn), .out(multiplexer_1_out), .sel(t_ff_2_qn));
  RAM #(.addrWidth(16), .dataWidth(16)) LOW (
    .addr(ADDR), .we(controlled_buffer_1_out), .oe(multiplexer_1_out), .clk(clk), .din(DATA), .dout(LOW_dout));
  RAM #(.addrWidth(16), .dataWidth(16)) HIGH (
    .addr(ADDR), .we(controlled_buffer_1_out), .oe(multiplexer_1_out), .clk(clk), .din(DATA), .dout(HIGH_dout));
  S_R_Flip_Flop s_r_ff_1 (.S(multiplexer_1_out), .R(1'b0), .clk(clk));  // open: Q, reset, Qn, preset
  D_Flip_Flop d_ff_1 (.Q(d_ff_1_q));  // open: D, clk, Qn, preset, reset
  Pull_Resistor pull_resistor_2 (.node(cpuclk));
  assign cpuclk = d_ff_1_q ? clk : 1'bz;  // Controlled_Buffer controlled_buffer_2
  Demultiplexer #(.width(32)) demultiplexer_1 (
    .out0(rom_1_data), .out1({HIGH_dout, LOW_dout}), .in(DATAOUT), .sel(t_ff_1_q));
endmodule

module GPUROM (
  input  [15:0] ADDR,
  input  RD,
  input  WR,
  input  [15:0] DATA,
  input  clk,
  output [7:0] XOUT,
  output [7:0] YOUT,
  output WROUT,
  output [3:0] CLR
);

  wire and_1_out, comparator_1_eq, comparator_2_eq, comparator_3_eq, comparator_4_eq,
       controlled_buffer_1_out, controlled_buffer_2_out, not_1_out, not_2_out, or_1_out, or_2_out, or_3_out,
       s_r_ff_1_q, s_r_ff_3_qn, s_r_ff_4_q, subtractor_1_bout, t_ff_1_q, TILE_carry, undriven_2, undriven_3,
       undriven_4, X_carry, Y_carry;
  wire [2:0] TILE_q;
  wire [6:0] ram_1_dout, undriven;
  wire [7:0] rom_2_data;
  wire [9:0] adder_2_out, ADDRCNT_q, counter_1_q, multiplexer_1_out, multiplexer_2_out, multiplexer_3_out,
       register_1_q, subtractor_1_out;
  wire [11:0] adder_1_out, rom_1_data, Y_q;

  Multiplexer #(.width(10)) multiplexer_1 (
    .in0(ADDRCNT_q), .in1(counter_1_q), .out(multiplexer_1_out), .sel(s_r_ff_1_q));
  RAM #(.addrWidth(10), .dataWidth(7), .enables("line")) ram_1 (
    .addr(multiplexer_1_out), .we(undriven_3), .clk(clk), .din(undriven), .dout(ram_1_dout));
  S_R_Flip_Flop s_r_ff_1 (.S(WR), .clk(clk), .Q(s_r_ff_1_q));  // open: R, reset, Qn, preset
  assign controlled_buffer_1_out = undriven_3 ? undriven_4 : 1'bz;  // Controlled_Buffer controlled_buffer_1
  Pull_Resistor pull_resistor_1 (.node(controlled_buffer_1_out));
  // Probe on multiplexer_3_out
  ROM #(.addrWidth(7), .dataWidth(12)) rom_1 (.addr(ram_1_dout), .data(rom_1_data));
  Comparator #(.mode("unsigned"), .width(7)) comparator_1 (
    .a(undriven), .b(7'b0001000), .eq(comparator_1_eq));  // open: gt, lt
  Multiplexer #(.width(10)) multiplexer_2 (
    .in0(subtractor_1_out), .in1(register_1_q), .out(multiplexer_2_out), .sel(subtractor_1_bout));
  Counter #(.max('h3ff), .width(10)) counter_1 (
    .count(undriven_2), .Q(counter_1_q), .clk(clk));  // open: load, D, carry, up, clr
  or or_1 (or_1_out, undriven_3, not_1_out);
  not not_1 (not_1_out, undriven_3);
  Multiplexer #(.width(10)) multiplexer_3 (
    .in0(register_1_q), .in1(multiplexer_2_out), .out(multiplexer_3_out), .sel(comparator_1_eq));
  not not_2 (not_2_out, Y_carry);
  Comparator #(.mode("unsigned"), .width(16)) comparator_2 (
    .a(ADDR), .b(16'hfd), .eq(comparator_2_eq));  // open: gt, lt
  S_R_Flip_Flop s_r_ff_2 (.S(not_1_out), .R(undriven_3), .clk(or_2_out), .Q(WROUT));  // open: reset, Qn, preset
  Counter #(.max('h3ff), .width(10)) ADDRCNT (
    .load(or_3_out), .D(multiplexer_3_out), .count(or_1_out), .Q(ADDRCNT_q), .clk(or_2_out));  // open: carry, up, clr
  or or_2 (or_2_out, controlled_buffer_1_out, TILE_carry);
  T_Flip_Flop t_ff_1 (.T(Y_carry), .clk(undriven_4), .Q(t_ff_1_q), .reset(not_2_out));  // open: Qn, preset
  Subtractor #(.width(10)) subtractor_1 (
    .a(ADDRCNT_q), .b(10'h1), .out(subtractor_1_out), .bout(subtractor_1_bout));  // open: bin
  S_R_Flip_Flop s_r_ff_3 (.S(t_ff_1_q), .R(not_2_out), .clk(undriven_4), .Qn(s_r_ff_3_qn));  // open: Q, reset, preset
  Adder #(.width(12)) adder_1 (.a(rom_1_data), .b(Y_q), .out(adder_1_out));  // open: cin, cout
  Counter #(.max('h8), .width(12)) Y (.Q(Y_q), .carry(Y_carry), .clk(X_carry));  // open: load, D, count, up, clr
  and and_1 (and_1_out, ~WROUT, not_1_out);  // AND_Gate
  or or_3 (or_3_out, comparator_1_eq, X_carry, Y_carry, and_1_out);
  ROM #(.addrWidth(12)) rom_2 (.addr(adder_1_out), .data(rom_2_data));
  assign controlled_buffer_2_out = s_r_ff_3_qn ? t_ff_1_q : 1'bz;  // Controlled_Buffer controlled_buffer_2
  Counter #(.max('h7), .width(3)) TILE (
    .load(TILE_carry), .D(3'b000), .count(not_1_out), .Q(TILE_q), .carry(TILE_carry), .clk(undriven_4));  // open: up, clr
  Pull_Resistor pull_resistor_2 (.node(controlled_buffer_2_out));
  Counter X (.count(s_r_ff_4_q), .Q(XOUT), .carry(X_carry), .clk(undriven_4));  // open: load, D, up, clr
  Register #(.width(10)) register_1 (
    .D(adder_2_out), .en(controlled_buffer_2_out), .clk(undriven_4), .Q(register_1_q));  // open: clr
  Comparator #(.width(12)) comparator_3 (.a(Y_q), .b(12'h7), .eq(comparator_3_eq));  // open: gt, lt
  Adder #(.width(10)) adder_2 (.a(register_1_q), .b(10'h20), .out(adder_2_out));  // open: cin, cout
  // Shift_Register shift_register_1: pin names not known; wires that end beside it: TILE_carry, TILE_carry, WROUT, clk, 1'b0, CLR[3], CLR[3]
  S_R_Flip_Flop s_r_ff_4 (.S(comparator_4_eq), .R(1'b0), .clk(undriven_4), .Q(s_r_ff_4_q));  // open: reset, Qn, preset
  Comparator #(.mode("unsigned"), .width(3)) comparator_4 (
    .a(TILE_q), .b(3'b111), .eq(comparator_4_eq));  // open: gt, lt
  Counter counter_2 (.Q(YOUT), .clk(X_carry));  // open: load, D, count, carry, up, clr

  assign CLR[2:0] = {3{CLR[3]}};

  // Notes on the sheet:
  //   contents of rom_1 (hex, n*v repeats v):
  //   97*0 10 18
  //   contents of rom_2 (hex, n*v repeats v):
  //   16*0 1c 22 41 7f 41 41 41 0 7e 41 41 7e 41 41 7e
endmodule

module PIC (
  input  RES,
  input  INTR_0,
  input  INTR_1,
  input  INTR_2,
  input  INTR_3,
  input  INTR_4,
  input  INTR_5,
  input  INTR_6,
  input  INTR_7,
  input  CLK,
  input  [15:0] DATA,
  input  [15:0] ADDR,
  input  WR,
  output INT,
  output [15:0] INTO
);

  wire and_1_out, and_2_out, and_3_out, comparator_1_eq, comparator_2_eq, comparator_3_eq, comparator_4_eq,
       j_k_ff_1_q, j_k_ff_1_qn, j_k_ff_2_q, priority_encoder_1_gs;
  wire [2:0] multiplexer_1_out, priority_encoder_1_out, register_1_q;

  Priority_Encoder priority_encoder_1 (
    .in0(INTR_0), .in1(INTR_1), .in2(INTR_2), .in3(INTR_3), .in4(INTR_4), .in5(INTR_5), .in6(INTR_6),
    .in7(INTR_7), .out(priority_encoder_1_out), .en_in(j_k_ff_1_q), .gs(priority_encoder_1_gs));  // open: en_out
  and and_1 (and_1_out, comparator_3_eq, comparator_1_eq, WR);
  and and_2 (and_2_out, WR, comparator_2_eq, comparator_3_eq);
  Comparator #(.mode("unsigned"), .width(16)) comparator_1 (
    .a(DATA), .b({16{1'b1}}), .eq(comparator_1_eq));  // open: gt, lt
  Comparator #(.mode("unsigned"), .width(16)) comparator_2 (
    .a(DATA), .b(16'hfffe), .eq(comparator_2_eq));  // open: gt, lt
  Comparator #(.mode("unsigned"), .width(16)) comparator_3 (
    .a(ADDR), .b(16'hfffc), .eq(comparator_3_eq));  // open: gt, lt
  Comparator #(.mode("unsigned"), .width(16)) comparator_4 (
    .a(ADDR), .b(16'hfffd), .eq(comparator_4_eq));  // open: gt, lt
  and and_3 (and_3_out, comparator_4_eq, WR);
  J_K_Flip_Flop j_k_ff_1 (
    .J(and_1_out), .K(and_2_out), .clk(CLK), .Q(j_k_ff_1_q), .Qn(j_k_ff_1_qn), .reset(RES));  // open: preset
  J_K_Flip_Flop j_k_ff_2 (.J(and_3_out), .K(j_k_ff_2_q), .clk(CLK), .Q(j_k_ff_2_q));  // open: Qn, preset, reset
  Register #(.width(3)) register_1 (.D(ADDR[2:0]), .en(and_3_out), .clk(CLK), .Q(register_1_q));  // open: clr
  Multiplexer #(.width(3)) multiplexer_1 (
    .in0(priority_encoder_1_out), .in1(register_1_q), .out(multiplexer_1_out), .sel(j_k_ff_1_qn));
  RAM #(.addrWidth(3), .clearpin("true"), .dataWidth(16)) ram_1 (
    .addr(multiplexer_1_out), .we(j_k_ff_2_q), .oe(priority_encoder_1_gs), .clk(CLK), .din(ADDR),
    .dout(INTO), .clr(RES));
  D_Flip_Flop d_ff_1 (.D(priority_encoder_1_gs), .clk(CLK), .Q(INT));  // open: Qn, preset, reset
endmodule
