// Logisim project GPUtest.circ as structural Verilog
module DRAW (
  input  clk,
  output [7:0] XO,
  output [7:0] YO,
  output XOE,
  output YOE
);

  Counter X (.Q(XO), .carry(XOE), .clk(clk));  // open: load, D, count, up, clr
  Counter Y (.count(XOE), .Q(YO), .carry(YOE), .clk(clk));  // open: load, D, up, clr
endmodule

module TEXTMODE (
  input  [7:0] CLR,
  input  [9:0] ASCII,
  input  RD,
  input  [7:0] X,
  input  [7:0] Y,
  input  XO,
  input  YO,
  input  clk,
  input  OE,
  output [7:0] TEXTDATA
);

  wire comparator_1_eq, counter_1_carry, counter_2_carry, shift_register_1_p5;
  wire [2:0] counter_2_q;
  wire [7:0] multiplexer_1_out;
  wire [63:0] rom_1_data;

  ROM #(.addrWidth(10), .dataWidth(64)) rom_1 (.addr(ASCII), .data(rom_1_data));
  Counter #(.max('h7), .width(3)) counter_1 (
    .count(RD), .carry(counter_1_carry), .clk(clk));  // open: load, D, Q, up, clr
  // Shift_Register shift_register_1: pin names not known; wires that end beside it: counter_1_carry, 1'b1, clk, 1'b0, shift_register_1_p5, 1'b0
  Multiplexer #(.select(3), .width(8)) multiplexer_1 (
    .in0(rom_1_data[63:56]), .in1(rom_1_data[55:48]), .in2(rom_1_data[47:40]), .in3(rom_1_data[39:32]),
    .in4(rom_1_data[31:24]), .in5(rom_1_data[23:16]), .in6(rom_1_data[15:8]), .in7(rom_1_data[7:0]),
    .out(multiplexer_1_out), .sel(counter_2_q));
  Counter #(.max('h7), .width(3)) counter_2 (
    .load(counter_2_carry), .D(3'b000), .count(1'b1), .Q(counter_2_q), .carry(counter_2_carry), .up(1'b1),
    .clk(XO));  // open: clr
  Multiplexer #(.enable("true"), .width(8)) multiplexer_2 (
    .in0(CLR), .in1({8{1'b0}}), .out(TEXTDATA), .sel(comparator_1_eq), .en(OE));
  Comparator #(.mode("unsigned"), .width(1)) comparator_1 (
    .a(shift_register_1_p5), .b(1'b0), .eq(comparator_1_eq));  // open: gt, lt

  // Notes on the sheet:
  //   contents of rom_1 (hex, n*v repeats v):
  //   0 1c22417f41414100 7e41417e41417e00
endmodule

module GPU (
);

  wire draw_1_xoe, draw_1_yoe, undriven;
  wire [7:0] draw_1_xo, draw_1_yo;
  wire [9:0] mem_1_char;

  DRAW draw_1 (.clk(undriven), .XO(draw_1_xo), .YO(draw_1_yo), .XOE(draw_1_xoe), .YOE(draw_1_yoe));
  MEM mem_1 (.CHAR(mem_1_char));  // open: ASCII
  TEXTMODE textmode_1 (
    .ASCII(mem_1_char), .X(draw_1_xo), .Y(draw_1_yo), .XO(draw_1_xoe), .YO(draw_1_yoe), .clk(undriven));  // open: CLR, RD, OE, TEXTDATA
endmodule

module MEM (
  input  [6:0] ASCII,
  output [9:0] CHAR
);

  RAM VRAM ();  // open: addr, we, oe, clk, din, dout
  ROM #(.addrWidth(16)) MICROCODE ();  // open: addr, data
  ROM #(.addrWidth(7), .dataWidth(10)) CHARROM (.addr(ASCII), .data(CHAR));
  ROM GPROM ();  // open: addr, data
endmodule

module Bitmap (
);

  Register X ();  // open: D, en, clk, Q, clr
  Register Y ();  // open: D, en, clk, Q, clr
  Register X1 ();  // open: D, en, clk, Q, clr
  Register Y1 ();  // open: D, en, clk, Q, clr
endmodule

module LINE (
  input  OE,
  input  clk,
  input  [7:0] X1,
  input  [7:0] Y1,
  input  [7:0] X2,
  input  [7:0] Y2
);

  wire and_1_out, and_2_out, and_3_out, comparator_1_gt, comparator_1_lt, comparator_2_gt, comparator_2_lt,
       comparator_3_eq, comparator_3_lt, comparator_4_eq, comparator_4_gt, comparator_5_lt, comparator_6_lt,
       controlled_buffer_1_out, d_ff_1_q, d_ff_1_qn, multiplexer_1_out, multiplexer_2_out, nor_1_out,
       not_1_out, subtractor_1_bout, subtractor_2_bout, xor_1_out;
  wire [7:0] adder_1_out, adder_2_out, multiplexer_3_out, multiplexer_4_out, multiplexer_5_out,
       multiplexer_6_out, multiplexer_7_out, multiplexer_8_out, subtractor_1_out, subtractor_2_out, X_q, Y_q;

  D_Flip_Flop d_ff_1 (.D(OE), .clk(clk), .Q(d_ff_1_q), .Qn(d_ff_1_qn));  // open: preset, reset
  Subtractor subtractor_1 (.a(Y2), .b(Y1), .out(subtractor_1_out), .bout(subtractor_1_bout));  // open: bin
  Subtractor subtractor_2 (.a(X2), .b(X1), .out(subtractor_2_out), .bout(subtractor_2_bout));  // open: bin
  xor xor_1 (xor_1_out, subtractor_1_bout, subtractor_2_bout);
  Multiplexer multiplexer_1 (.in0(comparator_1_gt), .in1(comparator_1_lt), .out(multiplexer_1_out), .sel(xor_1_out));
  Comparator #(.mode("unsigned")) comparator_1 (
    .a(X1), .b(X2), .gt(comparator_1_gt), .lt(comparator_1_lt));  // open: eq
  Multiplexer multiplexer_2 (.in0(comparator_2_gt), .in1(comparator_2_lt), .out(multiplexer_2_out), .sel(xor_1_out));
  Comparator #(.mode("unsigned")) comparator_2 (
    .a(Y1), .b(Y2), .gt(comparator_2_gt), .lt(comparator_2_lt));  // open: eq
  Multiplexer #(.width(8)) multiplexer_3 (
    .in0(adder_1_out), .in1(multiplexer_5_out), .out(multiplexer_3_out), .sel(d_ff_1_qn));
  Multiplexer #(.width(8)) multiplexer_4 (
    .in0(adder_2_out), .in1(multiplexer_6_out), .out(multiplexer_4_out), .sel(d_ff_1_qn));
  Adder adder_1 (.a(subtractor_1_out), .b(Y_q), .out(adder_1_out));  // open: cin, cout
  Register Y (.D(multiplexer_3_out), .en(OE), .clk(clk), .Q(Y_q));  // open: clr
  Register X (.D(multiplexer_4_out), .en(OE), .clk(clk), .Q(X_q));  // open: clr
  Adder adder_2 (.a(subtractor_2_out), .b(X_q), .out(adder_2_out));  // open: cin, cout
  and and_1 (and_1_out, multiplexer_1_out, multiplexer_2_out);
  not not_1 (not_1_out, and_1_out);
  Multiplexer #(.width(8)) multiplexer_5 (.in0(Y1), .in1(Y2), .out(multiplexer_5_out), .sel(and_1_out));
  Multiplexer #(.width(8)) multiplexer_6 (.in0(X1), .in1(X2), .out(multiplexer_6_out), .sel(and_1_out));
  Multiplexer #(.width(8)) multiplexer_7 (.in0(Y1), .in1(Y2), .out(multiplexer_7_out), .sel(not_1_out));
  Multiplexer #(.width(8)) multiplexer_8 (.in0(X1), .in1(X2), .out(multiplexer_8_out), .sel(not_1_out));
  and and_2 (and_2_out, d_ff_1_q, and_3_out);
  Comparator comparator_3 (.a(Y_q), .b(multiplexer_7_out), .eq(comparator_3_eq), .lt(comparator_3_lt));  // open: gt
  Comparator comparator_4 (.a(X_q), .b(multiplexer_8_out), .gt(comparator_4_gt), .eq(comparator_4_eq));  // open: lt
  and and_3 (and_3_out, comparator_3_eq, comparator_4_eq);
  Comparator comparator_5 (.a(Y_q), .b(multiplexer_5_out), .lt(comparator_5_lt));  // open: gt, eq
  Comparator comparator_6 (.a(multiplexer_8_out), .b(X_q), .lt(comparator_6_lt));  // open: gt, eq
  nor nor_1 (nor_1_out, comparator_6_lt, comparator_5_lt, comparator_4_gt, comparator_3_lt);
  assign controlled_buffer_1_out = nor_1_out ? OE : 1'bz;  // Controlled_Buffer controlled_buffer_1
  // RGB_Video #(.height(256), .scale(1), .width(256)) rgb_video_1: pin names not known; wires that end beside it: comparator_6_lt, comparator_5_lt, comparator_4_gt, comparator_3_lt, clk, controlled_buffer_1_out, X_q, Y_q, {24{1'b0}}
  Pull_Resistor pull_resistor_1 (.node(controlled_buffer_1_out));
endmodule
